// Logisim project cpu.circ as structural Verilog: 1 circuit, main circuit cpu
module cpu (
  input  Rest
);

  wire alu_1_p5, alucontroller_1_p1, alucontroller_1_p2, and_1_out, and_2_out, and_3_out, and_4_out,
       and_5_out, clk, comparator_1_eq, comparator_2_eq, controller_1_p2, controller_1_p3, controller_1_p4,
       controller_1_p5, controller_1_p6, controller_1_p7, LB, multiplexer_2_out, not_1_out, RType;
  wire [1:0] alu_1_p4;
  wire [3:0] adder_1_out_2, controller_1_p9, multiplexer_8_out, shifter_4_out;
  wire [4:0] bit_extender_4_out, multiplexer_3_out, multiplexer_4_out, shifter_5_out;
  wire [7:0] multiplexer_12_out;
  wire [27:0] adder_1_out;
  wire [31:0] adder_2_out, alu_1_p8, bit_extender_1_out, bit_extender_2_out, bit_extender_3_out,
       bit_extender_5_out, mem_2_p1, multiplexer_1_out, multiplexer_5_out, multiplexer_6_out,
       multiplexer_7_out, multiplexer_9_out, multiplexer_11_out, multiplexer_13_out, multiplexer_14_out, pc,
       RegisterFile_p8, RegisterFile_p9, shifter_1_out, shifter_2_out, shifter_3_out, shifter_6_out,
       signextend_1_p2, xor_1_out;
  wire [31:2] alu_1_p4_2;

  Multiplexer #(.width(32)) multiplexer_1 (
    .in0(multiplexer_11_out), .in1({alu_1_p4_2, alu_1_p4}), .out(multiplexer_1_out), .sel(and_3_out));
  Multiplexer multiplexer_2 (.in0(1'b1), .in1(1'b0), .out(multiplexer_2_out), .sel(and_4_out));
  Clock u_Clk (.out(clk));
  Register #(.width(32)) u_PC (.D(multiplexer_1_out), .en(multiplexer_2_out), .clk(clk), .Q(pc), .clr(Rest));
  Adder #(.width(32)) adder_1 (.a(32'h4), .b(pc), .out({adder_1_out_2, adder_1_out}));  // open: cin, cout
  // mem mem_1: pin names not known; wires that end beside it: pc, clk
  Multiplexer #(.width(5)) multiplexer_3 (
    .in0(5'b00001), .in1({5{1'b0}}), .out(multiplexer_3_out), .sel(controller_1_p2));
  assign bit_extender_1_out = {{6{1'b0}}, 26'h10003};  // Bit_Extender bit_extender_1
  and and_1 (and_1_out, controller_1_p4, controller_1_p5);
  Multiplexer #(.width(5)) multiplexer_4 (
    .in0(multiplexer_3_out), .in1({5{1'b1}}), .out(multiplexer_4_out), .sel(and_1_out));
  Multiplexer #(.width(32)) multiplexer_5 (
    .in0(multiplexer_14_out), .in1(pc), .out(multiplexer_5_out), .sel(and_1_out));
  Shifter #(.width(32)) shifter_1 (.in(bit_extender_1_out), .\dist (5'b00010), .out(shifter_1_out));
  assign bit_extender_2_out = {{28{1'b0}}, adder_1_out_2};  // Bit_Extender bit_extender_2
  assign bit_extender_3_out = {{27{1'b0}}, {5{1'b0}}};  // Bit_Extender bit_extender_3
  Shifter #(.width(32)) shifter_2 (.in(bit_extender_2_out), .\dist (5'b11100), .out(shifter_2_out));
  // Controller controller_1: pin names not known; wires that end beside it: 6'b101000, controller_1_p2, controller_1_p3, controller_1_p4, controller_1_p5, controller_1_p6, controller_1_p7, RType, controller_1_p9
  assign xor_1_out = shifter_1_out ^ shifter_2_out;  // XOR_Gate xor_1, 32 bits wide
  // regfile RegisterFile: pin names not known; wires that end beside it: {5{1'b0}}, 5'b00001, multiplexer_4_out, multiplexer_5_out, controller_1_p5, clk, LB, RegisterFile_p8, RegisterFile_p9
  // signExtend signextend_1: pin names not known; wires that end beside it: 16'h3, signextend_1_p2, 6'b000011, 6'b101000, RType
  and and_2 (and_2_out, ~controller_1_p3, controller_1_p6);  // AND_Gate
  Multiplexer #(.width(32)) multiplexer_6 (
    .in0(RegisterFile_p8), .in1(bit_extender_3_out), .out(multiplexer_6_out), .sel(alucontroller_1_p2));
  Shifter #(.width(32)) shifter_3 (.in(signextend_1_p2), .\dist (5'b00010), .out(shifter_3_out));
  Multiplexer #(.width(32)) multiplexer_7 (
    .in0(RegisterFile_p9), .in1(signextend_1_p2), .out(multiplexer_7_out), .sel(and_2_out));
  assign bit_extender_4_out = {{3{1'b0}}, alu_1_p4};  // Bit_Extender bit_extender_4
  // AluController alucontroller_1: pin names not known; wires that end beside it: alucontroller_1_p1, alucontroller_1_p2
  and and_3 (and_3_out, alu_1_p5, ~comparator_2_eq, RType);  // AND_Gate
  Adder #(.width(32)) adder_2 (
    .a({adder_1_out_2, adder_1_out}), .b(shifter_3_out), .out(adder_2_out));  // open: cin, cout
  Comparator #(.width(4)) comparator_1 (.a(controller_1_p9), .b(4'b0001), .eq(comparator_1_eq));  // open: gt, lt
  Shifter #(.width(4)) shifter_4 (.in(controller_1_p9), .\dist (alu_1_p4), .out(shifter_4_out));
  Shifter #(.width(5)) shifter_5 (.in(bit_extender_4_out), .\dist (3'b011), .out(shifter_5_out));
  and and_4 (and_4_out, RType, alu_1_p5, comparator_2_eq);
  Multiplexer #(.width(4)) multiplexer_8 (
    .in0(controller_1_p9), .in1(shifter_4_out), .out(multiplexer_8_out), .sel(comparator_1_eq));
  // ALU alu_1: pin names not known; wires that end beside it: multiplexer_6_out, multiplexer_7_out, alucontroller_1_p1, {alu_1_p4_2, alu_1_p4}, alu_1_p5, {alu_1_p4_2, alu_1_p4}, multiplexer_8_out, alu_1_p8, clk
  Shifter #(.width(32)) shifter_6 (.in(RegisterFile_p9), .\dist (shifter_5_out), .out(shifter_6_out));
  Multiplexer #(.width(32)) multiplexer_9 (
    .in0({adder_1_out_2, adder_1_out}), .in1(adder_2_out), .out(multiplexer_9_out), .sel(and_5_out));
  and and_5 (and_5_out, controller_1_p3, alu_1_p5);
  Multiplexer #(.width(32)) multiplexer_10 (
    .in0(RegisterFile_p9), .in1(shifter_6_out), .out(alu_1_p8), .sel(comparator_1_eq));
  Multiplexer #(.width(32)) multiplexer_11 (
    .in0(xor_1_out), .in1(multiplexer_9_out), .out(multiplexer_11_out), .sel(not_1_out));
  not not_1 (not_1_out, controller_1_p4);
  Comparator #(.width(32)) comparator_2 (
    .a({alu_1_p4_2, alu_1_p4}), .b({32{1'b1}}), .eq(comparator_2_eq));  // open: gt, lt
  // mem mem_2: pin names not known; wires that end beside it: mem_2_p1
  assign bit_extender_5_out = {{24{1'b1}}, multiplexer_12_out};  // Bit_Extender bit_extender_5
  Multiplexer #(.select(2), .width(8)) multiplexer_12 (
    .in0(mem_2_p1[7:0]), .in1(mem_2_p1[15:8]), .in2(mem_2_p1[23:16]), .in3(mem_2_p1[31:24]),
    .out(multiplexer_12_out), .sel(alu_1_p4));
  Multiplexer #(.width(32)) multiplexer_13 (
    .in0(mem_2_p1), .in1(bit_extender_5_out), .out(multiplexer_13_out), .sel(LB));
  Multiplexer #(.width(32)) multiplexer_14 (
    .in0({alu_1_p4_2, alu_1_p4}), .in1(multiplexer_13_out), .out(multiplexer_14_out), .sel(controller_1_p7));
endmodule
